# Fritzing sketch 1.a.ii.1-relay-driver (saved by Fritzing 0.9.0b)
breadboards: 1

parts:
  U1 = RELAY [package=relay-g5q]
  M1 = DC Motor

nets:
  N1: U1.MAIN, M1.pin_1

notes:
  3V
  5V
  .21A
  .3A
