# Fritzing sketch 1.a.ii.2-transistor-driver (saved by Fritzing 0.9.0b)
breadboards: 1

parts:
  Q1 = Basic FET N-Channel [package="TO220 [THT]"]
  M1 = DC Motor

nets:
  N1: Q1.drain, M1.pin_2

notes:
  5.0V
  1.0V
  0.0A
  .17A
