# Fritzing sketch circuit-1 (saved by Fritzing 0.9.0b)
breadboards: 1

parts:
  U1 = SWITCH_SPDT [package=kps-1290]
  BAT1 = Battery Holders [package=battery-aaa]
  LED1 = LEDs [package=led10mm]

nets:
  N1: U1.P, BAT1.-
  N2: U1.S, LED1.C
  N3: BAT1.+, LED1.A
