# Fritzing sketch circuit-6 (saved by Fritzing 0.9.0b)
breadboards: 1

parts:
  R3 = Resistor [tolerance=±5% resistance=5k package="0805 [SMD]"]
  R4 = PHOTOCELL [package=photocell-kit]

nets:
  N1: R3.Pin_1, R4.P$1
