# Fritzing sketch switch-with-pull-up (saved by Fritzing 0.9.0b)
breadboards: 1

parts:
  R3 = Resistor [tolerance=±5% resistance=5.6k package="0805 [SMD]"]
  S1 = Toggle Switch [package=THT]

nets:
  N1: R3.Pin_1, S1.COM
