# Fritzing sketch voltage-divider (saved by Fritzing 0.9.0b)
breadboards: 1

parts:
  R1 = Resistor [tolerance=±5% resistance=5.6k package="0805 [SMD]"]
  R2 = PHOTOCELL [package=photocell-kit]

nets:
  N1: R1.Pin_1, R2.P$1
