# Fritzing sketch 1.a.i.6.switch-with-current-limit-resistor (saved by Fritzing 0.9.0b)
breadboards: 1

parts:
  R3 = Resistor [tolerance=±5% resistance=5k package="0805 [SMD]"]
  LED1 = LED - 5mm [color="Red (633nm)" package="5 mm [THT]"]

nets:
  N1: R3.Pin_0, LED1.anode
