# Fritzing sketch circuit-7 (saved by Fritzing 0.9.0b)
breadboards: 1

parts:
  R3 = Resistor [tolerance=±5% resistance=5k package="0805 [SMD]"]
  U1 = POT [package=pot_mammoth]

nets:
  N1: R3.Pin_1, U1.S
