# Fritzing sketch 1.a.i.11_voltage-regulation-step-down (saved by Fritzing 0.9.0b)
breadboards: 1

parts:
  V2 = DC Power [voltage=15V]
  Part9 = Pololu 12V Step-Down Regulator

nets:
  N1: V2.V+, Part9.VIN
  N2: V2.V-, Part9.GND

notes:
  15V
  Touch to VOUT
  Touch to ground
  12V Step-down Regulator
