# Fritzing sketch 1.a.i.11_voltage-regulation-step-up-step-down (saved by Fritzing 0.9.0b)
breadboards: 1

parts:
  V1 = DC Power [voltage=3V]
  V2 = DC Power [voltage=9V]
  Part7 = 5V Step-up-ustep-down regulator
  Part8 = 5V Step-up-ustep-down regulator

nets:
  N1: V1.V+, Part8.VIN
  N2: V1.V-, Part8.GND
  N3: V2.V+, Part7.VIN
  N4: V2.V-, Part7.GND

notes:
  3V
  9V
  Touch to VOUT
  Touch to ground
  5V Step-Up/Step-Down Regulator
