# Fritzing sketch 1.a.i.11_voltage-regulation (saved by Fritzing 0.9.0b)
breadboards: 1

parts:
  U1 = LIPO-2000mAh [package=lipo-2000]
  U5 = SPX29302 [package=q5-dd_spx29300]
  Part1 = Pololu 12V Step-Down Regulator
  Part2 = Pololu 5V Step-Up Regulator
  V1 = DC Power [voltage=5]
  V2 = DC Power [voltage=5]

nets:
  N1: U1.+, Part2.VIN
  N2: U1.-, Part2.GND
  N3: U5.VIN, V2.V+
  N4: U5.GND, V2.V-
  N5: Part1.VIN, Part1.SHDN, V1.V+
  N6: Part1.GND, V1.V-

notes:
  12V
  5V
  5V step-down
  5V step-up
  variable voltage regulator
  Touch to VOUT
  Touch to ground
