# Fritzing sketch 1.a.i.5_switch-with-pullup (saved by Fritzing 0.9.0b)
breadboards: 1

parts:
  S1 = Toggle Switch [package=THT]
  V1 = DC Power [voltage=5]
  Voltmeter1 = Voltmeter
  R3 = Resistor [tolerance=±5% resistance=5.6k package="0805 [SMD]"]

nets:
  N1: S1.COM, Voltmeter1.Positive, R3.Pin_1
  N2: S1.L2, V1.V-, Voltmeter1.Com
  N3: V1.V+, R3.Pin_0

custom parts:
  Voltmeter: A Standard Multimeter in Current mode
