# Fritzing sketch 1.a.i.8_pressure-pad-with-bias-resistor (saved by Fritzing 0.9.0b)
breadboards: 1

parts:
  R2 = Resistor [package="0402 [SMD]"]
  Voltmeter1 = Voltmeter
  V1 = DC Power [voltage=5]
  R1 = Resistor [package="0402 [SMD]"]

nets:
  N1: R2.Pin_0, Voltmeter1.Positive, R1.Pin_1
  N2: R2.Pin_1, V1.V-
  N3: Voltmeter1.Com, V1.V+, R1.Pin_0

notes:
  5V
  2.4V
  conductive fabric
  bias resistor

custom parts:
  Voltmeter: A Standard Multimeter in Current mode
