# Fritzing sketch 1.a.i.9_transducer-with-dmm (saved by Fritzing 0.9.0b)
breadboards: 1

parts:
  Part1 = Humidity Sensor - HIH-4030 Breakout
  V1 = DC Power [voltage=5]
  Voltmeter1 = Voltmeter

nets:
  N1: Part1.GND, V1.V-, Voltmeter1.Positive
  N2: Part1.OUT, Voltmeter1.Com
  N3: Part1.VCC, V1.V+

notes:
  5.0V
  0.0A
  1.3V

custom parts:
  Voltmeter: A Standard Multimeter in Current mode
