# Fritzing sketch 1.a.ii.1_relay-driver (saved by Fritzing 0.9.0b)
breadboards: 1

parts:
  V1 = DC Power [voltage=5]
  V2 = DC Power [voltage=3V]
  M1 = DC Motor
  LED1 = smd LED [color="Red (633nm)" package="0805 [SMD]"]
  U2 = RELAY [package=relay-g5q]
  R1 = Resistor [tolerance=±5% resistance=220 package="0805 [SMD]"]

nets:
  N1: V1.V+, U2.COIL1
  N2: V1.V-, U2.COIL2
  N3: V2.V+, U2.COM
  N4: V2.V-, M1.pin_2, LED1.cathode
  N5: M1.pin_1, U2.NO
  N6: LED1.anode, R1.Pin_0
  N7: U2.NC, R1.Pin_1

notes:
  3V
  5V
  .21A
  .3A

custom parts:
  RELAY: HASCO KLT1C6DC5
