# Fritzing sketch 1.a.ii.3_multichannel-driver (saved by Fritzing 0.9.0b)
breadboards: 1

parts:
  M3 = DC Motor
  M4 = DC Motor
  V1 = DC Power [voltage=5]
  IC1 = ULN2803A [package=THT]

nets (from the schematic view):
  N1: M3.pin_1, M4.pin_1, V1.V+, IC1.COM_-_Common
  N2: M3.pin_2, IC1.Out_7
  N3: M4.pin_2, IC1.Out_8
  N4: V1.V-, IC1.0V

notes:
  5V
  5V here to turn on motor
