# Fritzing sketch 1.a.ii.4-transistor-and-sensor-for-power (saved by Fritzing 0.9.0b)
breadboards: 1

parts:
  M1 = DC Motor
  Q1 = TRANSISTOR_PNP [package=to-92]
  V1 = DC Power [voltage=5]
  R1 = PHOTOCELL [package=photocell-kit]

nets (from the schematic view):
  N1: M1.pin_1, Q1.C
  N2: M1.pin_2, V1.V-
  N3: Q1.E, V1.V+, R1.P$1
  N4: Q1.B, R1.P$2

notes:
  5.0V
  0.1A
