# Fritzing sketch 1.a.ii.4_transistor-and-sensor-for-power (saved by Fritzing 0.9.0b)
breadboards: 1

parts:
  R1 = PHOTOCELL [package=photocell-kit]
  Q2 = NPN-Transistor [package="TO92 [THT]"]
  M1 = DC Motor
  V1 = DC Power [voltage=5]
  V2 = DC Power [voltage=2]

nets:
  N1: R1.P$1, V1.V+
  N2: R1.P$2, Q2.B
  N3: Q2.E, V1.V-, V2.V-
  N4: Q2.C, M1.pin_2
  N5: M1.pin_1, V2.V+

notes:
  2.0V
  .17A
  5.0V
  .01A
  2N3904
