# Fritzing sketch 1.b.ii.2_blink-motor (saved by Fritzing 0.9.0b)
breadboards: 1

parts:
  Part1 = Arduino Uno (Rev3)
  Q1 = PNP-Transistor [package="TO92 [THT]"]
  V1 = DC Power [voltage=12V]
  M1 = DC Motor

nets:
  N1: Part1.D13/SCK, Q1.B
  N2: Part1.GND, Q1.C, V1.V-
  N3: Q1.E, M1.pin_2
  N4: V1.V+, M1.pin_1

notes:
  12.0V
  .02A
