# Fritzing sketch 1.b.ii.2_blink-motor (saved by Fritzing 0.9.0b)
breadboards: 1

parts:
  V1 = DC Power [voltage=12V]  # not connected
  Part2 = Arduino Uno (Rev3)
  Q2 = NPN-Transistor [package="TO92 [THT]"]
  M1 = DC Motor  # not connected

nets:
  N1: Part2.D13/SCK, Q2.C
  N2: Part2.GND, Q2.E

notes:
  12.0V
  .02A
