# Fritzing sketch 1.b.ii.3_analog-read-serial (saved by Fritzing 0.9.0b)
breadboards: 1

parts:
  Part1 = Ambi
  Part2 = Arduino Uno (Rev3)

nets:
  VCC: Part1.VCC, Part2.5V
  GND: Part1.GND, Part2.GND
  N1: Part1.V0, Part2.A0

notes:
  Analog Ambient Light Sensor
