# Fritzing sketch 1.b.ii.4_digital-read-serial (saved by Fritzing 0.9.0b)
breadboards: 1

parts:
  Part1 = Arduino Uno (Rev3) - ICSP
  S1 = Toggle Switch [package=THT]

nets:
  N1: Part1.D2, S1.COM
  N2: Part1.GND, S1.L2
