# Fritzing sketch 1.b.ii.4_digital-read-serial (saved by Fritzing 0.9.0b)
breadboards: 1

parts:
  Part1 = Arduino Uno (Rev3) - ICSP
  S1 = Toggle Switch [package=THT]
  R1 = Resistor [tolerance=±5% resistance=10k package=THT]

nets:
  N1: Part1.5V, R1.Pin_1
  N2: Part1.GND, S1.L2
  N3: Part1.D2, S1.COM, R1.Pin_0
