# Fritzing sketch 1.b.ii.5_servo-sweep (saved by Fritzing 0.9.0b)

parts:
  Part1 = Arduino Uno (Rev3)
  J1 = Basic Servo

nets:
  N1: Part1.D8, J1.pulse
  GND: Part1.GND, J1.gnd
  5V: Part1.5V, J1.vcc
