# Fritzing sketch 1.b.ii.6_motor-knob (saved by Fritzing 0.9.0b)
breadboards: 1

parts:
  DRV1 = A4983
  Part1 = Arduino Uno (Rev3)
  M2 = Stepper Motor - Bipolar
  R1 = TRIMPOT [package=trimpot_pth_s3_lock]
  R3 = Resistor [tolerance=±5% resistance=10k package="1206 [SMD]"]
  R4 = Resistor [tolerance=±5% resistance=10k package="1206 [SMD]"]
  V1 = DC Power [voltage=9]
  R5 = Resistor [tolerance=±5% resistance=10k package="1206 [SMD]"]
  R6 = Resistor [tolerance=±5% resistance=10k package="1206 [SMD]"]

nets:
  N1: DRV1.EN, R6.Pin_0
  N2: DRV1.MS1, R5.Pin_0
  N3: DRV1.RST, R4.Pin_0
  N4: DRV1.SLP, R3.Pin_0
  N5: DRV1.STEP, Part1.D3_PWM
  N6: DRV1.DIR, Part1.D2
  N7: DRV1.VMOT, V1.V+
  N8: DRV1.GNDMOT, V1.V-
  N9: DRV1.2B, M2.A
  N10: DRV1.2A, M2.C
  N11: DRV1.1A, M2.B
  N12: DRV1.1B, M2.D
  VDD: DRV1.VDD, Part1.5V, R1.CCW, R3.Pin_1, R4.Pin_1, R5.Pin_1, R6.Pin_1
  GND: DRV1.GND, Part1.GND, R1.CW
  N13: Part1.A0, R1.WIPER

notes:
  5V
  .36A

custom parts:
  A4983: Poloko A4983 Stepper Motor Control Breakout
