# Fritzing sketch 1.b.ii.6_stepper-motor-knob (saved by Fritzing 0.9.0b)
breadboards: 1

parts:
  Part1 = Arduino Uno (Rev3)
  M2 = Stepper Motor - Bipolar
  R1 = TRIMPOT [package=trimpot_pth_s3_lock]
  R3 = Resistor [tolerance=±5% resistance=10k package="1206 [SMD]"]
  R4 = Resistor [tolerance=±5% resistance=10k package="1206 [SMD]"]
  V1 = DC Power [voltage=9]
  R5 = Resistor [tolerance=±5% resistance=10k package="1206 [SMD]"]
  R6 = Resistor [tolerance=±5% resistance=10k package="1206 [SMD]"]
  DRV1 = A4983

nets:
  N1: Part1.A0, R1.WIPER
  N2: Part1.D2, DRV1.DIR
  N3: Part1.D3_PWM, DRV1.STEP
  5V: Part1.5V, R1.CCW, R3.Pin_1, R4.Pin_1, R5.Pin_1, R6.Pin_1, DRV1.VDD
  GND: Part1.GND, R1.CW, DRV1.GND
  N4: M2.A, DRV1.2B
  N5: M2.C, DRV1.2A
  N6: M2.B, DRV1.1A
  N7: M2.D, DRV1.1B
  N8: R3.Pin_0, DRV1.SLP
  N9: R4.Pin_0, DRV1.RST
  N10: V1.V+, DRV1.VMOT
  N11: V1.V-, DRV1.GNDMOT
  N12: R5.Pin_0, DRV1.MS1
  N13: R6.Pin_0, DRV1.EN

notes:
  5V
  .36A

custom parts:
  A4983: Poloko A4983 Stepper Motor Control Breakout
