# Fritzing sketch 1.c.ii.3_sensor-to-led (saved by Fritzing 0.9.0b)
breadboards: 1

parts:
  Part3 = Arduino Uno (Rev3)
  Part4 = Ambi
  LED1 = smd LED [color="Red (633nm)" package="0603 [SMD]"]
  R1 = Resistor [tolerance=±5% resistance=220 package=THT]

nets:
  N1: Part3.A0, Part4.V0
  N2: Part3.D3_PWM, R1.Pin_1
  5V: Part3.5V, Part4.VCC
  GND: Part3.GND, Part4.GND, LED1.cathode
  N3: LED1.anode, R1.Pin_0

notes:
  Analog Ambient Light Sensor
