# Fritzing sketch 1.c.ii.4_sensor-to-actuator (saved by Fritzing 0.9.0b)
breadboards: 1

parts:
  J1 = Basic Servo
  Part1 = Ambi
  Part2 = Arduino Uno (Rev3)
  V1 = DC Power [voltage=5]

nets:
  N1: J1.gnd, V1.V-
  N2: J1.vcc, V1.V+
  N3: J1.pulse, Part2.D4
  VCC: Part1.VCC, Part2.5V
  GND: Part1.GND, Part2.GND
  N4: Part1.V0, Part2.A0

notes:
  5V
