# Fritzing sketch 1.c.i_SensorToLED (saved by Fritzing 0.9.0b)
breadboards: 1

parts:
  Part3 = Arduino Uno (Rev3)
  Part4 = Ambi

nets:
  N1: Part3.A0, Part4.V0
  5V: Part3.5V, Part4.VCC

notes:
  Analog Ambient Light Sensor
