# Fritzing sketch 1.c.ii_SensorToLED (saved by Fritzing 0.9.0b)
breadboards: 1

parts:
  Part3 = Arduino Uno (Rev3)
  Part4 = Ambi
  LED1 = smd LED [color="Red (633nm)" package="0603 [SMD]"]

nets:
  N1: Part3.A0, Part4.V0
  GND: Part3.GND, Part4.GND, LED1.cathode
  N2: Part3.D2, LED1.anode
  5V: Part3.5V, Part4.VCC

notes:
  Analog Ambient Light Sensor
