# Fritzing sketch 1.c.iii.1_sensor-to-sound (saved by Fritzing 0.9.0b)
breadboards: 1

parts:
  Part1 = Arduino Uno (Rev3)
  Part2 = Ambi

nets:
  N1: Part1.A0, Part2.V0
  GND: Part1.GND, Part2.GND
  5V: Part1.5V, Part2.VCC
