# Fritzing sketch 1.c.iii_sensor-to-actuator (saved by Fritzing 0.9.0b)
breadboards: 1

parts:
  J1 = Basic Servo
  Part1 = Ambi
  Part2 = Arduino Uno (Rev3)

nets:
  GND: J1.gnd, Part1.GND, Part2.GND
  VCC: J1.vcc, Part1.VCC, Part2.5V
  N1: J1.pulse, Part2.D2
  N2: Part1.V0, Part2.A0
