# Fritzing sketch PrintAmbi (saved by Fritzing 0.9.0b)
breadboards: 1

parts:
  Part1 = UDOO
  Part3 = Ambi

nets:
  N1: Part1.A0, Part3.V0
  5V: Part1.5V, Part3.VCC
  GND: Part1.GND, Part3.GND

notes:
  5v
  GND
  A0
  X

custom parts:
  UDOO: The UDOO is a single-board computer development platform that merges a dual or quad core ARM Freescale Cortex-A9 i.MX.6 CPU and an Arduino compatible board embedded with a dedicated ARM Atmel SAM3X8E CPU.
