# Fritzing sketch PrintAccelerometer (saved by Fritzing 0.9.0b)
breadboards: 1

parts:
  Part1 = UDOO
  R1 = Photocell (LDR) [package=THT]
  R2 = Resistor [tolerance=±5% resistance=1k package="0805 [SMD]"]
  Part2 = Triple Axis Accelerometer Breakout - ADXL335  # not connected

nets:
  N1: Part1.A0, R1.pin_1, R2.Pin_0
  N2: Part1.5V, R1.pin_0
  N3: Part1.GND, R2.Pin_1

notes:
  5v
  GND
  1K

custom parts:
  UDOO: The UDOO is a single-board computer development platform that merges a dual or quad core ARM Freescale Cortex-A9 i.MX.6 CPU and an Arduino compatible board embedded with a dedicated ARM Atmel SAM3X8E CPU.
