# Fritzing sketch PrintReflectance (saved by Fritzing 0.9.0b)
breadboards: 1

parts:
  Part1 = UDOO
  Part2 = IRS01A

nets:
  N1: Part1.A0, Part2.OUT
  5V: Part1.5V, Part2.VIN
  GND: Part1.GND, Part2.GND

notes:
  5v
  GND
  A0
  X

custom parts:
  UDOO: The UDOO is a single-board computer development platform that merges a dual or quad core ARM Freescale Cortex-A9 i.MX.6 CPU and an Arduino compatible board embedded with a dedicated ARM Atmel SAM3X8E CPU.
  IRS01A: The QTR-1A reflectance sensor carries a single infrared LED and phototransistor pair in an inexpensive, tiny 0.5" x 0.3" module that can be mounted almost anywhere and is great for edge detection and line following. The reflectance measurement is output as an analog voltage. This sensor is sold in packs of two units.
