# Fritzing sketch PrintDigitalIn (saved by Fritzing 0.9.0b)
breadboards: 1

parts:
  Part3 = UDOO
  S1 = Pushbutton [package="[THT]"]

nets:
  N1: Part3.D8_PWM, S1.Pin_3, S1.Pin_4
  N2: Part3.GND, S1.Pin_1, S1.Pin_2

notes:
  GND
  8

custom parts:
  UDOO: The UDOO is a single-board computer development platform that merges a dual or quad core ARM Freescale Cortex-A9 i.MX.6 CPU and an Arduino compatible board embedded with a dedicated ARM Atmel SAM3X8E CPU.
