# Fritzing sketch tDCS-diagram (saved by Fritzing 0.9.0b)
breadboards: 1

parts:
  VCC1 = Battery block 9V
  LED1 = smd LED [color="Red (633nm)" package="1206 [SMD]"]
  R2 = Resistor [tolerance=±5% resistance=4k package=THT]
  S1 = SPST Switch [package=switch-spdt_kit]
  T2 = Adjustable Current Source [package="TO92 [THT]"]
  R3 = Rotary Potentiometer (Small) [maximum_resistance=100kΩ package=THT]
  R5 = Resistor [tolerance=±5% resistance=18.2 package="0805 [SMD]"]
  U1 = Self-Adhering Electrode
  U2 = Self-Adhering Electrode
  Digital_Panel_Meter_Voltage_DMS-20PC_by_Murata1 = Digital Panel Meter, Voltage, DMS-20PC  # not connected

nets:
  N1: VCC1.-, LED1.anode, U1.Wire
  N2: VCC1.+, S1.P
  N3: LED1.cathode, R2.Pin_0
  N4: R2.Pin_1, S1.S, T2.R
  N5: T2.V-, R3.leg1
  N6: R3.wiper, R5.Pin_0
  N7: R5.Pin_1, U2.Wire

custom parts:
  Adjustable Current Source: The LM134/LM234/LM334 are 3-terminal adjustable current sources featuring 10,000:1 range in operating current, excellent current regulation and a wide dynamic voltage range of 1V to 40V. Current is established with one external resistor and no other parts are required. Initial current accuracy is ±3%. The LM134/LM234/LM334 are true floating current sources with no separate power supply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
  Self-Adhering Electrode: Self-adhering electrode for tdcs.
